// Logisim project CPU.circ as structural Verilog
module main (
);

  Latch latch_1 ();  // open: st, v, out_3
endmodule

module MYXOR (
  input  a,
  input  b,
  output out
);

  wire and_1_out, and_2_out, not_1_out, not_2_out;

  not not_1 (not_1_out, a);
  not not_2 (not_2_out, b);
  and and_1 (and_1_out, not_1_out, b);
  and and_2 (and_2_out, a, not_2_out);
  or or_1 (out, and_1_out, and_2_out);
endmodule

module HALF_ADDER (
  input  a,
  input  b,
  output o,
  output c
);

  xor xor_1 (o, a, b);
  and and_1 (c, a, b);
endmodule

module FULL_ADDER (
  input  _1,
  input  _2,
  input  _3,
  output o,
  output c
);

  wire half_adder_1_c, half_adder_1_o, half_adder_2_c;

  HALF_ADDER half_adder_1 (.a(_1), .b(_2), .o(half_adder_1_o), .c(half_adder_1_c));
  HALF_ADDER half_adder_2 (.a(half_adder_1_o), .b(_3), .o(o), .c(half_adder_2_c));
  or or_1 (c, half_adder_1_c, half_adder_2_c);
endmodule

module _16BitAdder (
  input  [15:0] in_1,
  input  [15:0] in_2,
  input  carry,
  output out_4,
  output [15:0] out_5
);

  wire n8bitadder_1_carry_2;

  _8BitAdder u_8bitadder_1 (
    .in_1(in_1[7:0]), .in_2(in_2[7:0]), .carry_2(n8bitadder_1_carry_2), .out(out_5[7:0]), .carry(carry));
  _8BitAdder u_8bitadder_2 (
    .in_1(in_1[15:8]), .in_2(in_2[15:8]), .carry_2(out_4), .out(out_5[15:8]), .carry(n8bitadder_1_carry_2));
endmodule

module _8BitAdder (
  input  [7:0] in_1,
  input  [7:0] in_2,
  input  carry,
  output [7:0] out,
  output carry_2
);

  wire full_adder_2_c, full_adder_3_c, full_adder_4_c, full_adder_5_c, full_adder_6_c, full_adder_7_c,
       full_adder_8_c;

  FULL_ADDER full_adder_1 (._1(full_adder_2_c), ._2(in_2[7]), ._3(in_1[7]), .o(out[7]), .c(carry_2));
  FULL_ADDER full_adder_2 (._1(full_adder_3_c), ._2(in_2[6]), ._3(in_1[6]), .o(out[6]), .c(full_adder_2_c));
  FULL_ADDER full_adder_3 (._1(full_adder_4_c), ._2(in_2[5]), ._3(in_1[5]), .o(out[5]), .c(full_adder_3_c));
  FULL_ADDER full_adder_4 (._1(full_adder_5_c), ._2(in_2[4]), ._3(in_1[4]), .o(out[4]), .c(full_adder_4_c));
  FULL_ADDER full_adder_5 (._1(full_adder_6_c), ._2(in_2[3]), ._3(in_1[3]), .o(out[3]), .c(full_adder_5_c));
  FULL_ADDER full_adder_6 (._1(full_adder_7_c), ._2(in_2[2]), ._3(in_1[2]), .o(out[2]), .c(full_adder_6_c));
  FULL_ADDER full_adder_7 (._1(full_adder_8_c), ._2(in_2[1]), ._3(in_1[1]), .o(out[1]), .c(full_adder_7_c));
  FULL_ADDER full_adder_8 (._1(carry), ._2(in_2[0]), ._3(in_1[0]), .o(out[0]), .c(full_adder_8_c));
endmodule

module DFF (
  input  st,
  input  cl,
  input  v,
  output out_4
);

  wire latch_1_out_3;

  Latch latch_1 (.st(st), .v(v), .out_3(latch_1_out_3));
  Latch latch_2 (.st(cl), .v(latch_1_out_3), .out_3(out_4));
endmodule

module Selector (
  input  in_1,
  input  in_2,
  input  in_3,
  output out_4
);

  wire and_1_out, and_2_out, not_1_out;

  not not_1 (not_1_out, in_1);
  and and_1 (and_1_out, in_1, in_2);
  and and_2 (and_2_out, not_1_out, in_3);
  or or_1 (out_4, and_1_out, and_2_out);
endmodule

module Latch (
  input  st,
  input  v,
  output out_3
);

  wire and_1_out, and_2_out, nor_2_out, not_1_out;

  not not_1 (not_1_out, v);
  and and_1 (and_1_out, not_1_out, st);
  and and_2 (and_2_out, st, v);
  nor nor_1 (out_3, and_1_out, nor_2_out);
  nor nor_2 (nor_2_out, and_2_out, out_3);
endmodule

module RAM (
  input  [7:0] in_1,
  input  in_2,
  input  in_3,
  input  in_4,
  output out_5,
  output [7:0] out_6
);

  DFF dff_1 ();  // open: cl, v, out_4, st
  RAM_part #(.bus("separate")) ram_1 (.addr(in_1), .data(out_6), .clk(in_4), .ld(in_2));  // open: din, str, sel, clr
endmodule

module ALU (
  input  [15:0] add_a,
  input  [15:0] add_b,
  output [15:0] add_out
);

  _16BitAdder u_16bitadder_1 (.in_1(add_a), .in_2(add_b), .carry(1'b0), .out_5(add_out));  // open: out_4
endmodule

module Registers (
  input  [2:0] read_1,
  input  [2:0] read_2,
  input  [2:0] write_reg,
  input  write_enabled,
  input  clock,
  input  [15:0] write_value,
  output [15:0] read_1_out,
  output [15:0] read_2_out
);

  wire demultiplexer_1_out0, demultiplexer_1_out1, demultiplexer_1_out2, demultiplexer_1_out3,
       demultiplexer_1_out4, demultiplexer_1_out5, demultiplexer_1_out6, demultiplexer_1_out7, undriven;
  wire [15:0] demultiplexer_2_out0, demultiplexer_2_out1, demultiplexer_2_out2, demultiplexer_2_out3,
       demultiplexer_2_out4, demultiplexer_2_out5, demultiplexer_2_out6, demultiplexer_2_out7, register_1_q,
       register_2_q, register_3_q, register_4_q, register_5_q, register_6_q, register_7_q, register_8_q;

  Demultiplexer #(.select(3), .enable("false")) demultiplexer_1 (
    .out0(demultiplexer_1_out0), .out1(demultiplexer_1_out1), .out2(demultiplexer_1_out2),
    .out3(demultiplexer_1_out3), .out4(demultiplexer_1_out4), .out5(demultiplexer_1_out5),
    .out6(demultiplexer_1_out6), .out7(demultiplexer_1_out7), .in(write_enabled), .sel(write_reg));
  Demultiplexer #(.select(3), .width(16), .enable("false")) demultiplexer_2 (
    .out0(demultiplexer_2_out0), .out1(demultiplexer_2_out1), .out2(demultiplexer_2_out2),
    .out3(demultiplexer_2_out3), .out4(demultiplexer_2_out4), .out5(demultiplexer_2_out5),
    .out6(demultiplexer_2_out6), .out7(demultiplexer_2_out7), .in(write_value), .sel(write_reg));
  Multiplexer #(.select(3), .width(16), .enable("false")) multiplexer_1 (
    .in0(register_8_q), .in1(register_7_q), .in2(register_6_q), .in3(register_5_q), .in4(register_4_q),
    .in5(register_3_q), .in6(register_2_q), .in7(register_1_q), .out(read_1_out), .sel(read_1));
  Register #(.width(16)) register_1 (
    .D(demultiplexer_2_out7), .en(demultiplexer_1_out7), .Q(register_1_q), .clk(clock));  // open: clr
  Register #(.width(16)) register_2 (
    .D(demultiplexer_2_out6), .en(demultiplexer_1_out6), .Q(register_2_q), .clk(clock), .clr(undriven));
  Register #(.width(16)) register_3 (
    .D(demultiplexer_2_out5), .en(demultiplexer_1_out5), .Q(register_3_q), .clk(clock));  // open: clr
  Register #(.width(16)) register_4 (
    .D(demultiplexer_2_out4), .en(demultiplexer_1_out4), .Q(register_4_q), .clk(clock));  // open: clr
  Register #(.width(16)) register_5 (
    .D(demultiplexer_2_out3), .en(demultiplexer_1_out3), .Q(register_5_q), .clk(clock));  // open: clr
  Register #(.width(16)) register_6 (
    .D(demultiplexer_2_out2), .en(demultiplexer_1_out2), .Q(register_6_q), .clk(clock));  // open: clr
  Register #(.width(16)) register_7 (
    .D(demultiplexer_2_out1), .en(demultiplexer_1_out1), .Q(register_7_q), .clk(clock));  // open: clr
  Register #(.width(16)) register_8 (
    .D(demultiplexer_2_out0), .en(demultiplexer_1_out0), .Q(register_8_q), .clk(clock));  // open: clr
  Multiplexer #(.select(3), .width(16), .enable("false")) multiplexer_2 (
    .in0(register_8_q), .in1(register_7_q), .in2(register_6_q), .in3(register_5_q), .in4(register_4_q),
    .in5(register_3_q), .in6(register_2_q), .in7(register_1_q), .out(read_2_out), .sel(read_2));
endmodule

module CPU (
  input  Save_RAM,
  input  in_2
);

  wire and_1_out, and_2_out, and_5_out, clock_1_out, clock_2_goto_ram_2,
       clock_2_goto_ram_iinstruction_pointer, clock_2_inc, clock_2_load_ram_calcualte, clock_2_write,
       evaluator_1_isneg, evaluator_1_iszero, multiplexer_5_out, multiplexer_11_out, multiplexer_13_out,
       multiplexer_15_out, nor_1_out, or_1_out, register_3_q, register_4_q, register_5_q, register_7_q,
       undriven;
  wire [2:0] multiplexer_6_out, multiplexer_7_out, multiplexer_8_out, register_1_q_2;
  wire [8:0] register_1_q;
  wire [15:0] and_3_out, and_4_out, JSR___JSRR_out_5, multiplexer_1_out, multiplexer_2_out,
       multiplexer_3_out, multiplexer_4_out, multiplexer_9_out, multiplexer_10_out, multiplexer_12_out,
       multiplexer_14_out, multiplexer_16_out, multiplexer_17_out, n5bitnegto16_1_out_2,
       n9bitnegto16_1_out_2, n9bitnegto16_2_out_2, n9bitnegto16_3_out_2, n9bitnegto16_4_out_2,
       n11bitnegto16_1_out_2, n16bitadder_1_out_5, n16bitadder_2_out_5, n16bitadder_3_out_5,
       n16bitadder_4_out_5, n16bitadder_5_out_5, n16bitadder_6_out_5, n16bitadder_7_out_5, not_1_out,
       ram_1_data, register_2_q, register_6_q, registers_1_read_1_out, registers_1_read_2_out;
  wire [15:12] register_1_q_3;

  Register #(.width(16)) register_1 (
    .D(ram_1_data), .Q({register_1_q_3, register_1_q_2, register_1_q}), .clk(clock_2_load_ram_calcualte),
    .clr(Save_RAM));  // open: en
  and and_1 (and_1_out, register_1_q_2[0], register_7_q);
  _11BitNegTo16 u_11bitnegto16_1 (.in_1({register_1_q_2[1:0], register_1_q}), .out_2(n11bitnegto16_1_out_2));
  _9BitNegTo16 u_9bitnegto16_1 (.in_1(register_1_q), .out_2(n9bitnegto16_1_out_2));
  _9BitNegTo16 u_9bitnegto16_2 (.in_1(register_1_q), .out_2(n9bitnegto16_2_out_2));
  _9BitNegTo16 u_9bitnegto16_3 (.in_1(register_1_q), .out_2(n9bitnegto16_3_out_2));
  and and_2 (and_2_out, register_1_q_2[1], register_4_q);
  _16BitAdder u_16bitadder_1 (
    .in_1(register_6_q), .in_2(n9bitnegto16_3_out_2), .carry(1'b1), .out_5(n16bitadder_1_out_5));  // open: out_4
  _16BitAdder JSR___JSRR (
    .in_1(n11bitnegto16_1_out_2), .in_2(register_6_q), .carry(1'b1), .out_5(JSR___JSRR_out_5));  // open: out_4
  _16BitAdder u_16bitadder_2 (
    .in_1(register_6_q), .in_2({16{1'b0}}), .carry(1'b1), .out_5(n16bitadder_2_out_5));  // open: out_4
  _9BitNegTo16 u_9bitnegto16_4 (.in_1(register_1_q), .out_2(n9bitnegto16_4_out_2));
  _16BitAdder u_16bitadder_3 (
    .in_1(n9bitnegto16_4_out_2), .in_2(register_6_q), .carry(1'b1), .out_5(n16bitadder_3_out_5));  // open: out_4
  assign and_3_out = registers_1_read_1_out & {{11{1'b0}}, register_1_q[4:0]};  // AND_Gate and_3, 16 bits wide
  assign and_4_out = registers_1_read_1_out & registers_1_read_2_out;  // AND_Gate and_4, 16 bits wide
  assign not_1_out = ~registers_1_read_1_out;  // NOT_Gate not_1, 16 bits wide
  _5BitNegTo16 u_5bitnegto16_1 (.in_1(register_1_q[4:0]), .out_2(n5bitnegto16_1_out_2));
  _16BitAdder u_16bitadder_4 (
    .in_1(n5bitnegto16_1_out_2), .in_2(registers_1_read_1_out), .carry(1'b0), .out_5(n16bitadder_4_out_5));  // open: out_4
  _16BitAdder u_16bitadder_5 (
    .in_1(registers_1_read_1_out), .in_2(registers_1_read_2_out), .carry(1'b0), .out_5(n16bitadder_5_out_5));  // open: out_4
  Multiplexer #(.width(16), .enable("false")) multiplexer_1 (
    .in0(and_4_out), .in1(and_3_out), .out(multiplexer_1_out), .sel(register_1_q[5]));
  and and_5 (and_5_out, register_1_q_2[2], register_5_q, register_5_q);
  Multiplexer #(.width(16), .enable("false")) multiplexer_2 (
    .in0(registers_1_read_1_out), .in1(JSR___JSRR_out_5), .out(multiplexer_2_out), .sel(register_1_q_2[2]));
  Multiplexer #(.width(16), .enable("false")) multiplexer_3 (
    .in0(n16bitadder_5_out_5), .in1(n16bitadder_4_out_5), .out(multiplexer_3_out), .sel(register_1_q[5]));
  or or_1 (or_1_out, and_1_out, and_2_out, and_5_out);
  Clock_part clock_1 (.out(clock_1_out));
  Multiplexer #(.select(4), .width(16), .enable("false")) multiplexer_4 (
    .in1(multiplexer_3_out), .in2(ram_1_data), .in4(n16bitadder_2_out_5), .in5(multiplexer_1_out),
    .in9(not_1_out), .in14(n16bitadder_3_out_5), .out(multiplexer_4_out), .sel(register_1_q_3));  // open: in0, in3, in6, in7, in8, in10, in11, in12, in13, in15
  Multiplexer #(.select(4), .disabled(0), .enable("false")) multiplexer_5 (
    .in0(1'b0), .in1(1'b1), .in2(1'b1), .in4(1'b1), .in5(1'b1), .in9(1'b1), .in12(1'b0), .in14(1'b1),
    .out(multiplexer_5_out), .sel(register_1_q_3));  // open: in3, in6, in7, in8, in10, in11, in13, in15
  Multiplexer #(.select(4), .width(3), .disabled(0), .enable("false")) multiplexer_6 (
    .in0(3'b000), .in1(register_1_q_2), .in2(register_1_q_2), .in3(3'b000), .in4(3'b111),
    .in5(register_1_q_2), .in6(3'b000), .in7(3'b000), .in8(3'b000), .in9(register_1_q_2), .in10(3'b000),
    .in11(3'b000), .in12(3'b000), .in13(3'b000), .in14(register_1_q_2), .in15(3'b000),
    .out(multiplexer_6_out), .sel(register_1_q_3));
  Multiplexer #(.select(4), .width(3), .disabled(0), .enable("false")) multiplexer_7 (
    .in0(3'b000), .in1(register_1_q[8:6]), .in2(3'b000), .in3(register_1_q_2), .in4(register_1_q[8:6]),
    .in5(register_1_q[8:6]), .in6(3'b000), .in7(3'b000), .in8(3'b000), .in9(register_1_q[8:6]),
    .in10(3'b000), .in11(3'b000), .in12(register_1_q[8:6]), .in13(3'b000), .in14(3'b000), .in15(3'b000),
    .out(multiplexer_7_out), .sel(register_1_q_3));
  Multiplexer #(.select(4), .width(3), .disabled(0), .enable("false")) multiplexer_8 (
    .in0(3'b000), .in1(register_1_q[2:0]), .in2(3'b000), .in3(3'b000), .in4(3'b000), .in5(register_1_q[2:0]),
    .in6(3'b000), .in7(3'b000), .in8(3'b000), .in9(3'b000), .in10(3'b000), .in11(3'b000), .in12(3'b000),
    .in13(3'b000), .in14(3'b000), .in15(3'b000), .out(multiplexer_8_out), .sel(register_1_q_3));
  Multiplexer #(.select(4), .width(16), .disabled(0), .enable("false")) multiplexer_9 (
    .in0({16{1'b0}}), .in1({16{1'b0}}), .in2(n9bitnegto16_1_out_2), .in3(n9bitnegto16_2_out_2),
    .in4({16{1'b0}}), .in5({16{1'b0}}), .in6({16{1'b0}}), .in7({16{1'b0}}), .in8({16{1'b0}}),
    .in9({16{1'b0}}), .in10({16{1'b0}}), .in11({16{1'b0}}), .in12({16{1'b0}}), .in13({16{1'b0}}),
    .in14({16{1'b0}}), .in15({16{1'b0}}), .out(multiplexer_9_out), .sel(register_1_q_3));
  Multiplexer #(.select(4), .width(16), .disabled(0), .enable("false")) multiplexer_10 (
    .in0({16{1'b0}}), .in1({16{1'b0}}), .in2({16{1'b0}}), .in3(registers_1_read_1_out), .in4({16{1'b0}}),
    .in5({16{1'b0}}), .in6({16{1'b0}}), .in7({16{1'b0}}), .in8({16{1'b0}}), .in9({16{1'b0}}),
    .in10({16{1'b0}}), .in11({16{1'b0}}), .in12({16{1'b0}}), .in13({16{1'b0}}), .in14({16{1'b0}}),
    .in15({16{1'b0}}), .out(multiplexer_10_out), .sel(register_1_q_3));
  Multiplexer #(.select(4), .disabled(0), .enable("false")) multiplexer_11 (
    .in0(1'b0), .in1(1'b0), .in2(1'b0), .in3(1'b1), .in4(1'b0), .in5(1'b0), .in6(1'b0), .in7(1'b0),
    .in8(1'b0), .in9(1'b0), .in10(1'b0), .in11(1'b0), .in12(1'b0), .in13(1'b0), .in14(1'b0), .in15(1'b0),
    .out(multiplexer_11_out), .sel(register_1_q_3));
  Multiplexer #(.select(4), .width(16), .disabled(0), .enable("false")) multiplexer_12 (
    .in0({16{1'b0}}), .in1(multiplexer_3_out), .in2(ram_1_data), .in3({16{1'b0}}), .in4({16{1'b0}}),
    .in5({16{1'b0}}), .in6({16{1'b0}}), .in7({16{1'b0}}), .in8({16{1'b0}}), .in9({16{1'b0}}),
    .in10({16{1'b0}}), .in11({16{1'b0}}), .in12({16{1'b0}}), .in13({16{1'b0}}), .in14(n16bitadder_3_out_5),
    .in15({16{1'b0}}), .out(multiplexer_12_out), .sel(register_1_q_3));
  Multiplexer #(.select(4), .disabled(0), .enable("false")) multiplexer_13 (
    .in0(1'b0), .in1(1'b1), .in2(1'b1), .in3(1'b0), .in4(1'b0), .in5(1'b1), .in9(1'b0), .in14(1'b1),
    .out(multiplexer_13_out), .sel(register_1_q_3));  // open: in6, in7, in8, in10, in11, in12, in13, in15
  Multiplexer #(.select(4), .width(16), .disabled(0), .enable("false")) multiplexer_14 (
    .in0(n16bitadder_1_out_5), .in1(16'he), .in2(16'he), .in3(16'he), .in4(multiplexer_2_out), .in5(16'he),
    .in6(16'he), .in7(16'he), .in8(16'he), .in9(16'he), .in10(16'he), .in11(16'he),
    .in12(registers_1_read_1_out), .in13(16'he), .in14(16'he), .in15(16'he), .out(multiplexer_14_out),
    .sel(register_1_q_3));
  Multiplexer #(.select(4), .disabled(0), .enable("false")) multiplexer_15 (
    .in0(or_1_out), .in1(1'b0), .in2(1'b0), .in3(1'b0), .in4(1'b1), .in5(undriven), .in6(undriven),
    .in7(undriven), .in8(undriven), .in9(undriven), .in10(undriven), .in11(undriven), .in12(1'b1),
    .in13(1'b0), .in14(1'b0), .in15(1'b0), .out(multiplexer_15_out), .sel(register_1_q_3));
  Clock clock_2 (
    .clocl(clock_1_out), .GOTO_RAM_iinstruction_pointer(clock_2_goto_ram_iinstruction_pointer),
    .LOAD_RAM_CALCUALTE(clock_2_load_ram_calcualte), .goto_ram_2(clock_2_goto_ram_2), .WRITE(clock_2_write),
    .INC(clock_2_inc));
  _16BitAdder u_16bitadder_6 (
    .in_1(register_6_q), .in_2(multiplexer_9_out), .carry(1'b1), .out_5(n16bitadder_6_out_5));  // open: out_4
  Registers registers_1 (
    .read_1(multiplexer_7_out), .read_2(multiplexer_8_out), .write_reg(multiplexer_6_out),
    .write_enabled(multiplexer_5_out), .clock(clock_2_write), .write_value(multiplexer_4_out),
    .read_1_out(registers_1_read_1_out), .read_2_out(registers_1_read_2_out));
  Multiplexer #(.width(16), .enable("false")) multiplexer_16 (
    .in0(register_6_q), .in1(n16bitadder_6_out_5), .out(multiplexer_16_out), .sel(clock_2_goto_ram_2));
  Register #(.width(16)) register_2 (.D(multiplexer_14_out), .Q(register_2_q), .clk(clock_2_write));  // open: en, clr
  Register #(.width(1)) register_3 (.D(multiplexer_15_out), .Q(register_3_q), .clk(clock_2_write));  // open: en, clr
  RAM_part #(.addrWidth(16), .dataWidth(16), .bus("separate")) ram_1 (
    .addr(multiplexer_16_out), .din(multiplexer_10_out), .data(ram_1_data), .str(multiplexer_11_out),
    .clk(clock_2_write));  // open: sel, ld, clr
  Evaluator evaluator_1 (.in(multiplexer_12_out), .isneg(evaluator_1_isneg), .iszero(evaluator_1_iszero));
  Register #(.width(1)) register_4 (
    .D(evaluator_1_iszero), .en(multiplexer_13_out), .Q(register_4_q), .clk(clock_2_write));  // open: clr
  Register #(.width(1)) register_5 (
    .D(evaluator_1_isneg), .en(multiplexer_13_out), .Q(register_5_q), .clk(clock_2_write));  // open: clr
  Multiplexer #(.width(16), .enable("false")) multiplexer_17 (
    .in0(n16bitadder_7_out_5), .in1(register_2_q), .out(multiplexer_17_out), .sel(register_3_q));
  Register #(.width(16)) register_6 (
    .D(multiplexer_17_out), .en(1'b1), .Q(register_6_q), .clk(clock_2_inc), .clr(in_2));
  Register #(.width(1)) register_7 (
    .D(nor_1_out), .en(multiplexer_13_out), .Q(register_7_q), .clk(clock_2_write));  // open: clr
  nor nor_1 (nor_1_out, evaluator_1_iszero, evaluator_1_isneg);
  _16BitAdder u_16bitadder_7 (
    .in_1(register_6_q), .in_2(16'h1), .carry(1'b0), .out_5(n16bitadder_7_out_5));  // open: out_4

  // Notes on the sheet:
  //   ADD+ DR, SR, 1 IMM5 
  //   ST
  //   BR
  //   LEA
  //   ADD
  //   AND
  //   NOT 
  //   JMP/RET
  //   LD
  //   GO TO RAM CLOCK
  //   SAVE RAM CLOCK
  //   w value
  //   w enable
  //   w reg
  //   R1
  //   R2
  //   ram addr (offset)
  //   ram set value
  //   write mode
  //   eval val
  //   do eval?
  //   jump location
  //   do jump?
  //   CLOCK
  //   PC CLOCK
  //   SAVE JMP
  //   DO JMP?
  //   n
  //   flags
  //   z
  //   Program Counter
  //   p
endmodule

module _2BitAdder (
  input  [1:0] a,
  input  [1:0] b,
  input  carry,
  output [1:0] out,
  output out_5
);

  wire full_adder_2_c;

  FULL_ADDER full_adder_1 (._1(b[1]), ._2(a[1]), ._3(full_adder_2_c), .o(out[1]), .c(out_5));
  FULL_ADDER full_adder_2 (._1(b[0]), ._2(a[0]), ._3(carry), .o(out[0]), .c(full_adder_2_c));
endmodule

module Evaluator (
  input  [15:0] in,
  output isneg,
  output iszero
);

  Comparator #(.width(16)) comparator_1 (.a(in), .b({16{1'b0}}), .eq(iszero));  // open: gt, lt

  assign isneg = in[15];
endmodule

module _9BitNegTo16 (
  input  [8:0] in_1,
  output [15:0] out_2
);

  wire [8:0] not_1_out;
  wire [15:0] n16bitadder_1_out_5, n16bitadder_2_out_5, not_2_out;

  assign not_1_out = ~in_1;  // NOT_Gate not_1, 9 bits wide
  assign not_2_out = ~n16bitadder_1_out_5;  // NOT_Gate not_2, 16 bits wide
  _16BitAdder u_16bitadder_1 (
    .in_1(16'h1), .in_2({{7{1'b0}}, not_1_out}), .carry(1'b0), .out_5(n16bitadder_1_out_5));  // open: out_4
  _16BitAdder u_16bitadder_2 (
    .in_1(16'h1), .in_2(not_2_out), .carry(1'b0), .out_5(n16bitadder_2_out_5));  // open: out_4
  Multiplexer #(.width(16), .enable("false")) multiplexer_1 (
    .in0({{7{1'b0}}, in_1}), .in1(n16bitadder_2_out_5), .out(out_2), .sel(in_1[8]));
endmodule

module Clock (
  input  clocl,
  output GOTO_RAM_iinstruction_pointer,
  output LOAD_RAM_CALCUALTE,
  output goto_ram_2,
  output WRITE,
  output INC
);

  wire demultiplexer_1_out5;
  wire [7:0] n8bitadder_1_out, register_1_q;

  Register register_1 (.D(n8bitadder_1_out), .Q(register_1_q), .clk(clocl), .clr(demultiplexer_1_out5));  // open: en
  _8BitAdder u_8bitadder_1 (
    .in_1(register_1_q), .in_2({8{1'b0}}), .out(n8bitadder_1_out), .carry(1'b1));  // open: carry_2
  Demultiplexer #(.select(4), .enable("false")) demultiplexer_1 (
    .out0(GOTO_RAM_iinstruction_pointer), .out1(LOAD_RAM_CALCUALTE), .out2(goto_ram_2), .out3(WRITE),
    .out4(INC), .out5(demultiplexer_1_out5), .in(1'b1), .sel(register_1_q[3:0]));  // open: out6, out7, out8, out9, out10, out11, out12, out13, out14, out15
endmodule

module _5BitNegTo16 (
  input  [4:0] in_1,
  output [15:0] out_2
);

  wire [4:0] not_1_out;
  wire [15:0] n16bitadder_1_out_5, n16bitadder_2_out_5, not_2_out;

  assign not_1_out = ~in_1;  // NOT_Gate not_1, 5 bits wide
  assign not_2_out = ~n16bitadder_1_out_5;  // NOT_Gate not_2, 16 bits wide
  _16BitAdder u_16bitadder_1 (
    .in_1(16'h1), .in_2({{11{1'b0}}, not_1_out}), .carry(1'b0), .out_5(n16bitadder_1_out_5));  // open: out_4
  _16BitAdder u_16bitadder_2 (
    .in_1(16'h1), .in_2(not_2_out), .carry(1'b0), .out_5(n16bitadder_2_out_5));  // open: out_4
  Multiplexer #(.width(16), .enable("false")) multiplexer_1 (
    .in0({{11{1'b0}}, in_1}), .in1(n16bitadder_2_out_5), .out(out_2), .sel(in_1[4]));
endmodule

module _11BitNegTo16 (
  input  [10:0] in_1,
  output [15:0] out_2
);

  wire [10:0] not_1_out;
  wire [15:0] n16bitadder_1_out_5, n16bitadder_2_out_5, not_2_out;

  assign not_1_out = ~in_1;  // NOT_Gate not_1, 11 bits wide
  assign not_2_out = ~n16bitadder_1_out_5;  // NOT_Gate not_2, 16 bits wide
  _16BitAdder u_16bitadder_1 (
    .in_1(16'h1), .in_2({{5{1'b0}}, not_1_out}), .carry(1'b0), .out_5(n16bitadder_1_out_5));  // open: out_4
  _16BitAdder u_16bitadder_2 (
    .in_1(16'h1), .in_2(not_2_out), .carry(1'b0), .out_5(n16bitadder_2_out_5));  // open: out_4
  Multiplexer #(.width(16), .enable("false")) multiplexer_1 (
    .in0({{5{1'b0}}, in_1}), .in1(n16bitadder_2_out_5), .out(out_2), .sel(in_1[10]));
endmodule
